# Fritzing sketch iosconfsgiot (saved by Fritzing 0.9.3b)
breadboards: 1

parts:
  Teensy_3_1 = Teensy 3.1  # not connected
  USBUART1 = PL2303 USB UART Breakout
  Raspberry_Pi_B_rev1 = Raspberry Pi B rev1
  DHT1 = DHT22 Humidity and Temperature Sensor
  S1 = Pushbutton [package="[THT]"]
  R1 = Resistor [tolerance=±5% resistance=10k package="0402 [SMD]"]
  LED1 = LED - 3mm [color="Red (633nm)" package="3 mm [THT]"]
  LED2 = LED - 3mm [color="Yellow (595nm)" package="3 mm [THT]"]
  U1 = RELAY-SOLIDSTATE [package=relay-s108t02]
  R2 = Resistor [tolerance=±5% resistance=220 package="2010 [SMD]"]
  R3 = Resistor [tolerance=±5% resistance=220 package="2010 [SMD]"]
  R4 = Resistor [tolerance=±5% resistance=10k package="2010 [SMD]"]

nets:
  GND: USBUART1.GND, Raspberry_Pi_B_rev1.GND, R1.Pin_1, U1.-, R2.Pin_1, R3.Pin_1
  N1: Raspberry_Pi_B_rev1.3V3, S1.Pin_3, S1.Pin_4
  N2: Raspberry_Pi_B_rev1.GPIO_17, LED2.anode, U1.+
  N3: Raspberry_Pi_B_rev1.GPIO_21, LED1.anode
  N4: Raspberry_Pi_B_rev1.GPIO_22, S1.Pin_1, S1.Pin_2, R1.Pin_0
  N5: DHT1.VDD, R4.Pin_1
  N6: DHT1.DATA, R4.Pin_0
  N7: LED1.cathode, R2.Pin_0
  N8: LED2.cathode, R3.Pin_0

custom parts:
  PL2303 USB UART Breakout: PL2302 Usb Uart Breakout Board with Battery
